// Logisim project Project02.circ as structural Verilog
module Half_Adder (
  input  a,
  input  b,
  output sum,
  output carry
);

  xor xor_1 (sum, a, b);
  and and_1 (carry, a, b);
endmodule

module Full_Adder (
  input  a,
  input  b,
  input  c,
  output sum,
  output carry
);

  wire and_1_out, and_2_out, xor_1_out;

  xor xor_1 (xor_1_out, a, b);
  and and_1 (and_1_out, a, b);
  xor xor_2 (sum, xor_1_out, c);
  and and_2 (and_2_out, xor_1_out, c);
  or or_1 (carry, and_2_out, and_1_out);
endmodule

module Add_4 (
  input  a0,
  input  a1,
  input  a2,
  input  a3,
  input  b0,
  input  b1,
  input  b2,
  input  b3,
  output out0,
  output out1,
  output out2,
  output out3
);

  wire adder_1_cout, adder_2_cout, adder_3_cout;

  Adder #(.width(1)) adder_1 (.a(a0), .b(b0), .out(out0), .cout(adder_1_cout));  // open: cin
  Adder #(.width(1)) adder_2 (.a(a1), .b(b1), .out(out1), .cin(adder_1_cout), .cout(adder_2_cout));
  Adder #(.width(1)) adder_3 (.a(a2), .b(b2), .out(out2), .cin(adder_2_cout), .cout(adder_3_cout));
  Adder #(.width(1)) adder_4 (.a(a3), .b(b3), .out(out3), .cin(adder_3_cout));  // open: cout
endmodule

module Inc4 (
  input  [15:0] a0,
  output [15:0] out0
);

  Adder #(.width(16)) adder_1 (.a(a0), .b(16'h1), .out(out0));  // open: cin, cout
endmodule

module ALU (
  input  zx,
  input  nx,
  input  zy,
  input  ny,
  input  f,
  input  no,
  input  [15:0] x,
  input  [15:0] y,
  output [15:0] out,
  output zr,
  output ng
);

  wire [15:0] adder_1_out, and_1_out, multiplexer_1_out, multiplexer_2_out, multiplexer_3_out,
       multiplexer_4_out, multiplexer_5_out, not_1_out, not_2_out, not_3_out;

  Multiplexer #(.width(16), .enable("false")) multiplexer_1 (
    .in0(x), .in1({16{1'b0}}), .out(multiplexer_1_out), .sel(zx));
  assign not_1_out = ~multiplexer_1_out;  // NOT_Gate not_1, 16 bits wide
  Multiplexer #(.width(16), .enable("false")) multiplexer_2 (
    .in0(y), .in1({16{1'b0}}), .out(multiplexer_2_out), .sel(zy));
  assign not_2_out = ~multiplexer_2_out;  // NOT_Gate not_2, 16 bits wide
  Multiplexer #(.width(16), .enable("false")) multiplexer_3 (
    .in0(multiplexer_1_out), .in1(not_1_out), .out(multiplexer_3_out), .sel(nx));
  Multiplexer #(.width(16), .enable("false")) multiplexer_4 (
    .in0(multiplexer_2_out), .in1(not_2_out), .out(multiplexer_4_out), .sel(ny));
  assign and_1_out = multiplexer_3_out & multiplexer_4_out;  // AND_Gate and_1, 16 bits wide
  Adder #(.width(16)) adder_1 (.a(multiplexer_3_out), .b(multiplexer_4_out), .out(adder_1_out));  // open: cin, cout
  Multiplexer #(.width(16), .enable("false")) multiplexer_5 (
    .in0(and_1_out), .in1(adder_1_out), .out(multiplexer_5_out), .sel(f));
  Comparator #(.width(16)) comparator_1 (.a(out), .b({16{1'b0}}), .eq(zr), .lt(ng));  // open: gt
  Multiplexer #(.width(16), .enable("false")) multiplexer_6 (
    .in0(multiplexer_5_out), .in1(not_3_out), .out(out), .sel(no));
  assign not_3_out = ~multiplexer_5_out;  // NOT_Gate not_3, 16 bits wide

  // Notes on the sheet:
  //   m1
  //   m2
  //   n1
  //   n2
  //   m3
  //   m4
  //   a1
  //   add1
  //   m5
  //   n3
  //   c1
  //   m6
endmodule
