// Logisim project Project03.circ as structural Verilog
module SR_Flip_Flop (
  input  Set,
  input  Reset,
  output Q,
  output notQ
);

  nand nand_1 (Q, Set, notQ);
  nand nand_2 (notQ, Q, Reset);
endmodule

module D_type_Flip_Flop (
  input  Set,
  input  Reset,
  output Q,
  output notQ
);

  wire nand_1_out, nand_2_out, not_1_out;

  not not_1 (not_1_out, Set);
  nand nand_1 (nand_1_out, Set, Reset);
  nand nand_2 (nand_2_out, Reset, not_1_out);
  nand nand_3 (Q, nand_1_out, notQ);
  nand nand_4 (notQ, Q, nand_2_out);
endmodule

module Bit (
  input  in,
  input  load,
  output out
);

  wire nand_1_out, nand_2_out, nand_4_out, not_1_out;

  not not_1 (not_1_out, in);
  nand nand_1 (nand_1_out, in, load);
  nand nand_2 (nand_2_out, load, not_1_out);
  nand nand_3 (out, nand_1_out, nand_4_out);
  nand nand_4 (nand_4_out, out, nand_2_out);
endmodule

module RAM8 (
  input  [15:0] in_1,
  input  load,
  input  [2:0] address,
  output [15:0] out_4
);

  wire clock_1_out, demultiplexer_1_out0, demultiplexer_1_out1, demultiplexer_1_out2, demultiplexer_1_out3,
       demultiplexer_1_out4, demultiplexer_1_out5, demultiplexer_1_out6, demultiplexer_1_out7;
  wire [15:0] register_1_q, register_2_q, register_3_q, register_4_q, register_5_q, register_6_q,
       register_7_q, register_8_q;

  Clock clock_1 (.out(clock_1_out));
  Demultiplexer #(.select(3), .enable("false")) demultiplexer_1 (
    .out0(demultiplexer_1_out0), .out1(demultiplexer_1_out1), .out2(demultiplexer_1_out2),
    .out3(demultiplexer_1_out3), .out4(demultiplexer_1_out4), .out5(demultiplexer_1_out5),
    .out6(demultiplexer_1_out6), .out7(demultiplexer_1_out7), .in(load), .sel(address));
  Register #(.width(16)) register_1 (
    .D(in_1), .en(demultiplexer_1_out0), .Q(register_1_q), .clk(clock_1_out));  // open: clr
  Register #(.width(16)) register_2 (
    .D(in_1), .en(demultiplexer_1_out2), .Q(register_2_q), .clk(clock_1_out));  // open: clr
  Register #(.width(16)) register_3 (
    .D(in_1), .en(demultiplexer_1_out1), .Q(register_3_q), .clk(clock_1_out));  // open: clr
  Register #(.width(16)) register_4 (
    .D(in_1), .en(demultiplexer_1_out3), .Q(register_4_q), .clk(clock_1_out));  // open: clr
  Register #(.width(16)) register_5 (
    .D(in_1), .en(demultiplexer_1_out4), .Q(register_5_q), .clk(clock_1_out));  // open: clr
  Register #(.width(16)) register_6 (
    .D(in_1), .en(demultiplexer_1_out5), .Q(register_6_q), .clk(clock_1_out));  // open: clr
  Register #(.width(16)) register_7 (
    .D(in_1), .en(demultiplexer_1_out6), .Q(register_7_q), .clk(clock_1_out));  // open: clr
  Register #(.width(16)) register_8 (
    .D(in_1), .en(demultiplexer_1_out7), .Q(register_8_q), .clk(clock_1_out));  // open: clr
  Multiplexer #(.select(3), .width(16)) multiplexer_1 (
    .in0(register_1_q), .in1(register_3_q), .in2(register_2_q), .in3(register_4_q), .in4(register_5_q),
    .in5(register_6_q), .in6(register_7_q), .in7(register_8_q), .out(out_4), .sel(address));  // open: en
endmodule

module RAM64 (
  input  [15:0] in,
  input  load,
  input  [5:0] address,
  output [15:0] out_4
);

  wire clock_1_out, demultiplexer_1_out0, demultiplexer_1_out1, demultiplexer_1_out2, demultiplexer_1_out3,
       demultiplexer_1_out4, demultiplexer_1_out5, demultiplexer_1_out6, demultiplexer_1_out7;
  wire [15:0] ram_1_data, ram_2_data, ram_3_data, ram_4_data, ram_5_data, ram_6_data, ram_7_data, ram_8_data;

  Clock clock_1 (.out(clock_1_out));
  Demultiplexer #(.select(3), .enable("false")) demultiplexer_1 (
    .out0(demultiplexer_1_out0), .out1(demultiplexer_1_out1), .out2(demultiplexer_1_out2),
    .out3(demultiplexer_1_out3), .out4(demultiplexer_1_out4), .out5(demultiplexer_1_out5),
    .out6(demultiplexer_1_out6), .out7(demultiplexer_1_out7), .in(load), .sel(address[5:3]));
  RAM #(.addrWidth(3), .dataWidth(16), .bus("separate")) ram_1 (
    .addr(address[2:0]), .din(in), .data(ram_1_data), .str(demultiplexer_1_out0), .clk(clock_1_out));  // open: sel, ld, clr
  RAM #(.addrWidth(3), .dataWidth(16), .bus("separate")) ram_2 (
    .addr(address[2:0]), .din(in), .data(ram_2_data), .str(demultiplexer_1_out4), .clk(clock_1_out));  // open: sel, ld, clr
  Multiplexer #(.select(3), .width(16), .enable("false")) multiplexer_1 (
    .in0(ram_1_data), .in1(ram_3_data), .in2(ram_5_data), .in3(ram_7_data), .in4(ram_2_data),
    .in5(ram_4_data), .in6(ram_6_data), .in7(ram_8_data), .out(out_4), .sel(address[5:3]));
  RAM #(.addrWidth(3), .dataWidth(16), .bus("separate")) ram_3 (
    .addr(address[2:0]), .din(in), .data(ram_3_data), .str(demultiplexer_1_out1), .clk(clock_1_out));  // open: sel, ld, clr
  RAM #(.addrWidth(3), .dataWidth(16), .bus("separate")) ram_4 (
    .addr(address[2:0]), .din(in), .data(ram_4_data), .str(demultiplexer_1_out5), .clk(clock_1_out));  // open: sel, ld, clr
  RAM #(.addrWidth(3), .dataWidth(16), .bus("separate")) ram_5 (
    .addr(address[2:0]), .din(in), .data(ram_5_data), .str(demultiplexer_1_out2), .clk(clock_1_out));  // open: sel, ld, clr
  RAM #(.addrWidth(3), .dataWidth(16), .bus("separate")) ram_6 (
    .addr(address[2:0]), .din(in), .data(ram_6_data), .str(demultiplexer_1_out6), .clk(clock_1_out));  // open: sel, ld, clr
  RAM #(.addrWidth(3), .dataWidth(16), .bus("separate")) ram_7 (
    .addr(address[2:0]), .din(in), .data(ram_7_data), .str(demultiplexer_1_out3), .clk(clock_1_out));  // open: sel, ld, clr
  RAM #(.addrWidth(3), .dataWidth(16), .bus("separate")) ram_8 (
    .addr(address[2:0]), .din(in), .data(ram_8_data), .str(demultiplexer_1_out7), .clk(clock_1_out));  // open: sel, ld, clr
endmodule

module RAM512 (
  input  [15:0] in,
  input  load,
  input  [8:0] address,
  output [15:0] out_4
);

  wire clock_1_out, demultiplexer_1_out0, demultiplexer_1_out1, demultiplexer_1_out2, demultiplexer_1_out3,
       demultiplexer_1_out4, demultiplexer_1_out5, demultiplexer_1_out6, demultiplexer_1_out7;
  wire [15:0] ram_1_data, ram_2_data, ram_3_data, ram_4_data, ram_5_data, ram_6_data, ram_7_data, ram_8_data;

  Clock clock_1 (.out(clock_1_out));
  Demultiplexer #(.select(3), .enable("false")) demultiplexer_1 (
    .out0(demultiplexer_1_out0), .out1(demultiplexer_1_out1), .out2(demultiplexer_1_out2),
    .out3(demultiplexer_1_out3), .out4(demultiplexer_1_out4), .out5(demultiplexer_1_out5),
    .out6(demultiplexer_1_out6), .out7(demultiplexer_1_out7), .in(load), .sel(address[8:6]));
  RAM #(.addrWidth(6), .dataWidth(16), .bus("separate")) ram_1 (
    .addr(address[5:0]), .din(in), .data(ram_1_data), .str(demultiplexer_1_out0), .clk(clock_1_out));  // open: sel, ld, clr
  RAM #(.addrWidth(6), .dataWidth(16), .bus("separate")) ram_2 (
    .addr(address[5:0]), .din(in), .data(ram_2_data), .str(demultiplexer_1_out4), .clk(clock_1_out));  // open: sel, ld, clr
  Multiplexer #(.select(3), .width(16), .enable("false")) multiplexer_1 (
    .in0(ram_1_data), .in1(ram_3_data), .in2(ram_5_data), .in3(ram_7_data), .in4(ram_2_data),
    .in5(ram_4_data), .in6(ram_6_data), .in7(ram_8_data), .out(out_4), .sel(address[8:6]));
  RAM #(.addrWidth(6), .dataWidth(16), .bus("separate")) ram_3 (
    .addr(address[5:0]), .din(in), .data(ram_3_data), .str(demultiplexer_1_out1), .clk(clock_1_out));  // open: sel, ld, clr
  RAM #(.addrWidth(6), .dataWidth(16), .bus("separate")) ram_4 (
    .addr(address[5:0]), .din(in), .data(ram_4_data), .str(demultiplexer_1_out5), .clk(clock_1_out));  // open: sel, ld, clr
  RAM #(.addrWidth(6), .dataWidth(16), .bus("separate")) ram_5 (
    .addr(address[5:0]), .din(in), .data(ram_5_data), .str(demultiplexer_1_out2), .clk(clock_1_out));  // open: sel, ld, clr
  RAM #(.addrWidth(6), .dataWidth(16), .bus("separate")) ram_6 (
    .addr(address[5:0]), .din(in), .data(ram_6_data), .str(demultiplexer_1_out6), .clk(clock_1_out));  // open: sel, ld, clr
  RAM #(.addrWidth(6), .dataWidth(16), .bus("separate")) ram_7 (
    .addr(address[5:0]), .din(in), .data(ram_7_data), .str(demultiplexer_1_out3), .clk(clock_1_out));  // open: sel, ld, clr
  RAM #(.addrWidth(6), .dataWidth(16), .bus("separate")) ram_8 (
    .addr(address[5:0]), .din(in), .data(ram_8_data), .str(demultiplexer_1_out7), .clk(clock_1_out));  // open: sel, ld, clr
endmodule

module PC (
  input  [15:0] in,
  input  load,
  input  inc,
  input  reset,
  output [15:0] out
);

  wire clock_1_out, or_1_out, or_2_out, or_3_out;
  wire [15:0] adder_1_out, and_1_out, multiplexer_1_out, multiplexer_2_out, multiplexer_3_out, not_1_out;

  Clock clock_1 (.out(clock_1_out));
  assign not_1_out = ~in;  // NOT_Gate not_1, 16 bits wide
  assign and_1_out = in & not_1_out;  // AND_Gate and_1, 16 bits wide
  Multiplexer #(.width(16), .enable("false")) multiplexer_1 (
    .in0(multiplexer_3_out), .in1(multiplexer_2_out), .out(multiplexer_1_out), .sel(or_1_out));
  Multiplexer #(.width(16), .enable("false")) multiplexer_2 (
    .in0(in), .in1(and_1_out), .out(multiplexer_2_out), .sel(reset));
  or or_1 (or_1_out, reset, load);
  or or_2 (or_2_out, load, inc);
  or or_3 (or_3_out, or_2_out, reset);
  Register #(.width(16)) register_1 (.D(multiplexer_1_out), .en(or_3_out), .Q(out), .clk(clock_1_out));  // open: clr
  Adder #(.width(16)) adder_1 (.a(out), .b(16'h1), .out(adder_1_out));  // open: cin, cout
  Multiplexer #(.width(16), .enable("false")) multiplexer_3 (
    .in0(out), .in1(adder_1_out), .out(multiplexer_3_out), .sel(inc));
endmodule
